// Logisim project EXP3.circ as structural Verilog: 1 circuit, main circuit main
module main (
  input  A,
  input  B,
  input  in_3,
  input  in_4,
  input  A_2,
  input  B_2,
  input  C_in,
  input  in_8,
  input  in_9,
  input  in_10
);

  wire and_1_out, and_2_out, and_3_out, and_4_out, and_5_out, and_6_out, and_7_out, and_8_out, not_1_out,
       not_2_out, or_1_out, or_2_out, or_3_out, or_4_out, xor_1_out, xor_2_out, xor_3_out, xor_4_out,
       xor_5_out, xor_6_out;

  xor xor_1 (xor_1_out, A_2, B_2);
  and and_1 (and_1_out, A_2, B_2);
  and and_2 (and_2_out, A_2, C_in);
  and and_3 (and_3_out, B_2, C_in);
  xor xor_2 (xor_2_out, A, B);
  and and_4 (and_4_out, A, B);
  LED led_1 (.in(xor_2_out));
  LED led_2 (.in(and_4_out));
  xor xor_3 (xor_3_out, xor_1_out, C_in);
  or or_1 (or_1_out, and_1_out, and_2_out);
  LED led_3 (.in(xor_3_out));
  or or_2 (or_2_out, or_1_out, and_3_out);
  LED led_4 (.in(or_2_out));
  not not_1 (not_1_out, in_3);
  xor xor_4 (xor_4_out, in_3, in_4);
  buf and_5 (and_5_out, in_4);  // AND_Gate
  not not_2 (not_2_out, in_8);
  LED led_5 (.in(xor_4_out));
  LED led_6 (.in(and_5_out));
  xor xor_5 (xor_5_out, in_8, in_9);
  and and_6 (and_6_out, not_2_out, in_9);
  and and_7 (and_7_out, not_2_out, in_10);
  and and_8 (and_8_out, in_9, in_10);
  xor xor_6 (xor_6_out, xor_5_out, in_10);
  LED led_7 (.in(xor_6_out));
  or or_3 (or_3_out, and_6_out, and_7_out);
  or or_4 (or_4_out, or_3_out, and_8_out);
  LED led_8 (.in(or_4_out));

  // Notes on the sheet:
  //   half adder
  //   Full adder
  //   Sum(S)
  //   Carry(C)
  //   Sum(S)
  //   C-out
  //   half subtactor
  //   Full subtractor
endmodule
