// Logisim project exp 4.circ as structural Verilog: 1 circuit, main circuit main
module main (
  input  in_1,
  input  in_2,
  input  in_3,
  input  in_4,
  input  in_5,
  input  in_6,
  input  in_7,
  input  in_8,
  input  in_9,
  input  in_10,
  input  in_11,
  input  in_12,
  input  in_13,
  input  in_14,
  input  [1:0] in_15,
  input  [1:0] in_16
);

  wire demultiplexer_1_out0, demultiplexer_1_out1, demultiplexer_1_out2, demultiplexer_1_out3,
       demultiplexer_2_out0, demultiplexer_2_out1, multiplexer_1_out, multiplexer_2_out;

  Multiplexer multiplexer_1 (.in0(in_1), .in1(in_2), .out(multiplexer_1_out), .sel(in_4), .en(in_5));
  LED led_1 (.in(multiplexer_1_out));
  Multiplexer #(.select(2)) multiplexer_2 (
    .in0(in_8), .in1(in_9), .in2(in_11), .in3(in_12), .out(multiplexer_2_out), .sel(in_16), .en(in_13));
  LED led_2 (.in(multiplexer_2_out));
  Demultiplexer #(.select(2)) demultiplexer_1 (
    .out0(demultiplexer_1_out0), .out1(demultiplexer_1_out1), .out2(demultiplexer_1_out2),
    .out3(demultiplexer_1_out3), .in(in_10), .sel(in_15), .en(in_14));
  Demultiplexer demultiplexer_2 (
    .out0(demultiplexer_2_out0), .out1(demultiplexer_2_out1), .in(in_3), .sel(in_7), .en(in_6));
  LED led_3 (.in(demultiplexer_1_out0));
  LED led_4 (.in(demultiplexer_1_out1));
  LED led_5 (.in(demultiplexer_1_out2));
  LED led_6 (.in(demultiplexer_1_out3));
  LED led_7 (.in(demultiplexer_2_out0));
  LED led_8 (.in(demultiplexer_2_out1));
endmodule
