// Logisim project exp2.circ as structural Verilog: 1 circuit, main circuit main
module main (
  input  A,
  input  A_2,
  input  B,
  input  A_3,
  input  B_2,
  input  A_4,
  input  B_3,
  input  A_5,
  input  B_4,
  input  A_6,
  input  B_5,
  input  A_7,
  input  B_6
);

  wire and_1_out, nand_1_out, nor_1_out, not_1_out, or_1_out, xnor_1_out, xor_1_out;

  not not_1 (not_1_out, A);
  LED led_1 (.in(not_1_out));
  buf and_1 (and_1_out, B_2);  // AND_Gate
  or or_1 (or_1_out, A_5, B_4);
  nand nand_1 (nand_1_out, A_7, B_6);
  LED led_2 (.in(and_1_out));
  LED led_3 (.in(or_1_out));
  LED led_4 (.in(nand_1_out));
  nor nor_1 (nor_1_out, A_2, B);
  xor xor_1 (xor_1_out, A_4, B_3);
  xnor xnor_1 (xnor_1_out, A_6, B_5);
  LED led_5 (.in(nor_1_out));
  LED led_6 (.in(xor_1_out));
  LED led_7 (.in(xnor_1_out));

  // Notes on the sheet:
  //   NAND Gate
  //   NOT Gate
  //   AND Gate
  //   OR Gate
  //   Output 
  //   Output
  //   Output
  //   Output
  //   NOR Gate
  //   XOR Gate
  //   XNOR Gate
  //   Output
  //   Output
  //   Output
endmodule
