// Logisim project sequential circuits.circ as structural Verilog: 1 circuit, main circuit main
module main (
  input  in_1,
  input  in_2,
  input  in_3,
  input  in_4,
  input  in_5,
  input  in_6,
  input  in_7,
  input  in_8,
  input  in_9,
  output out_10,
  output out_11,
  output out_12,
  output out_13,
  output out_14,
  output out_15
);

  wire clock_1_out, clock_2_out, clock_3_out, clock_4_out, d_ff_1_q, d_ff_1_qn;

  Clock clock_1 (.out(clock_1_out));
  Clock clock_2 (.out(clock_2_out));
  D_Flip_Flop d_ff_1 (
    .clk(clock_1_out), .D(in_2), .Q(d_ff_1_q), .Qn(d_ff_1_qn), .en(in_4), .reset(in_5));  // open: preset
  J_K_Flip_Flop j_k_ff_1 (.J(in_7), .clk(clock_2_out), .K(in_9), .Q(out_12), .Qn(out_14));  // open: preset, en, reset
  LED led_1 (.in(d_ff_1_q));
  LED led_2 (.in(d_ff_1_qn));
  Clock clock_3 (.out(clock_3_out));
  Clock clock_4 (.out(clock_4_out));
  S_R_Flip_Flop s_r_ff_1 (
    .S(in_1), .clk(clock_3_out), .R(in_3), .Q(out_10), .Qn(out_11), .en(in_6));  // open: preset, reset
  T_Flip_Flop t_ff_1 (.clk(clock_4_out), .T(in_8), .Q(out_13), .Qn(out_15));  // open: preset, reset, en

  // Notes on the sheet:
  //   D flip flop
  //   Jk flip flop
  //   SR flip flop
  //   T flip flop
endmodule
